// Logisim project projet_etu.circ as structural Verilog: 9 circuits, main circuit main
module main (
  input  Reset,
  input  ResetRAM
);

  wire Clock, Clock_out, CTRL, Exec, Fetch, getcst_1_imm, Load, ramctrl_1_memload, ramctrl_1_memstore, Store,
       WriteReg;
  wire [2:0] GetOp;
  wire [15:0] Addr, alu_1_output, getcst_1_cst, JMP_Address, MemIN, PC, R0, R1, R2, R3, R4, R5, R6, R7,
       registres_1_out_sr1, registres_1_out_sr2;
  wire [31:0] bit_extender_1_out, IR, MemOUT;

  Clock u_Clock (.out(Clock_out));
  Seq seq_1 (.ClockOrig(Clock_out), .reset(Reset), .Fetch(Fetch), .Exec(Exec), .Clock(Clock));
  LED led_1 (.in(Clock_out));
  RegPC regpc_1 (.JMP_Address(JMP_Address), .Cond(1'b0), .CTRL(CTRL), .Clock(Exec), .Reset(Reset), .PC(PC));
  // Probe on PC
  GetAddr getaddr_1 (.PC(PC), .Addr(Addr), .Fetch(Fetch), .Load(Load), .Store(Store));
  // Probe on Addr
  LED led_2 (.in(Fetch));
  LED led_3 (.in(Exec));
  // Probe on MemIN
  assign bit_extender_1_out = {{16{MemIN[15]}}, MemIN};  // Bit_Extender bit_extender_1
  // Probe on PC
  // Probe on IR
  // DecodeIR decodeir_1: pin names not known; wires that end beside it: Load, Store, CTRL, GetOp, IR, WriteReg, JMP_Address
  RamCtrl ramctrl_1 (
    .Store(Store), .Fetch(Fetch), .Exec(Exec), .Load(Load), .MemStore(ramctrl_1_memstore),
    .MemLoad(ramctrl_1_memload), .Clock(Clock));
  // Probe on MemOUT
  RAM #(.addrWidth(16), .dataWidth(32), .bus("separate")) ram_1 (
    .addr(Addr), .din(bit_extender_1_out), .data(MemOUT), .str(ramctrl_1_memstore), .clk(ramctrl_1_memstore),
    .ld(ramctrl_1_memload), .clr(ResetRAM));  // open: sel
  // Probe on R0
  // Probe on R3
  // Probe on R6
  Register #(.width(32), .trigger("falling")) RegIR (.D(MemOUT), .Q(IR), .clk(Fetch), .clr(Reset));  // open: en
  // Probe on R1
  // Probe on R4
  // Probe on R7
  // Probe on IR
  // Probe on R2
  // Probe on R5
  // Probe on IR[8:6]
  // Probe on IR[11:9]
  // Probe on IR[14:12]
  // Probe on getcst_1_cst
  GetCst getcst_1 (.IR(IR), .Cst(getcst_1_cst), .Imm(getcst_1_imm));
  Registres registres_1 (
    .SR1(IR[11:9]), .IN(alu_1_output), .SR2(IR[14:12]), .WriteReg(WriteReg), .DR(IR[8:6]),
    .OUT_SR1(registres_1_out_sr1), .OUT_SR2(registres_1_out_sr2), .OUT_DR(MemIN), .R0(R0), .R1(R1), .R2(R2),
    .R3(R3), .R4(R4), .R5(R5), .R6(R6), .R7(R7), .Reset(Reset), .Clock(Exec));
  // Probe on registres_1_out_sr2
  // Probe on registres_1_out_sr1
  ALU alu_1 (
    .e2(GetOp), .Input1(registres_1_out_sr1), .Input2(registres_1_out_sr2), .Cst(getcst_1_cst),
    .Output(alu_1_output), .Imm(getcst_1_imm));
  // Probe on alu_1_output
  // Probe on R0
  // Probe on R1
  // Probe on R2
  // Probe on R3
  // Probe on R4
  // Probe on R5
  // Probe on R6
  // Probe on R7
  // Probe on alu_1_output

  // Notes on the sheet:
  //   RAM
endmodule

module ALU (
  input  [2:0] e2,
  input  [15:0] Input1,
  input  [15:0] Input2,
  input  [15:0] Cst,
  input  Imm,
  output [15:0] Output
);

  wire decoder_1_out0, decoder_1_out1, decoder_1_out2, decoder_1_out3, decoder_1_out4, decoder_1_out5,
       decoder_1_out6, decoder_1_out7, not_1_out, not_2_out, or_2_out;
  wire [3:0] controlled_buffer_1_out;
  wire [15:0] adder_1_out, and_1_out, controlled_buffer_8_out, controlled_buffer_13_out, multiplier_1_out,
       or_1_out, shifter_1_out, shifter_2_out, subtractor_1_out, xor_1_out;
  wire [15:4] controlled_buffer_1_out_2;

  not not_1 (not_1_out, Imm);
  assign {controlled_buffer_1_out_2, controlled_buffer_1_out} = not_1_out ? Input2 : 16'bz;  // Controlled_Buffer controlled_buffer_1
  Adder #(.width(16)) adder_1 (
    .a({controlled_buffer_1_out_2, controlled_buffer_1_out}), .b(Input1), .out(adder_1_out));  // open: cin, cout
  Subtractor #(.width(16)) subtractor_1 (
    .a({controlled_buffer_1_out_2, controlled_buffer_1_out}), .b(Input1), .out(subtractor_1_out));  // open: bin, bout
  assign and_1_out = {controlled_buffer_1_out_2, controlled_buffer_1_out} & Input1;  // AND_Gate and_1, 16 bits wide
  assign or_1_out = {controlled_buffer_1_out_2, controlled_buffer_1_out} | Input1;  // OR_Gate or_1, 16 bits wide
  Shifter #(.width(16)) shifter_1 (.in(Input1), .\dist (controlled_buffer_1_out), .out(shifter_1_out));
  Shifter #(.width(16), .shift("lr")) shifter_2 (.in(Input1), .\dist (controlled_buffer_1_out), .out(shifter_2_out));
  Multiplier #(.width(16)) multiplier_1 (
    .a({controlled_buffer_1_out_2, controlled_buffer_1_out}), .b(Input1), .out(multiplier_1_out));  // open: cin, cout
  assign {controlled_buffer_1_out_2, controlled_buffer_1_out} = Imm ? Cst : 16'bz;  // Controlled_Buffer controlled_buffer_2
  assign Output = decoder_1_out0 ? adder_1_out : 16'bz;  // Controlled_Buffer controlled_buffer_3
  assign Output = decoder_1_out1 ? subtractor_1_out : 16'bz;  // Controlled_Buffer controlled_buffer_4
  assign Output = decoder_1_out2 ? and_1_out : 16'bz;  // Controlled_Buffer controlled_buffer_5
  assign xor_1_out = {controlled_buffer_1_out_2, controlled_buffer_1_out} ^ Input1;  // XOR_Gate xor_1, 16 bits wide
  or or_2 (or_2_out, controlled_buffer_1_out_2[4], controlled_buffer_1_out_2[5], controlled_buffer_1_out_2[6], controlled_buffer_1_out_2[7], controlled_buffer_1_out_2[8], controlled_buffer_1_out_2[9], controlled_buffer_1_out_2[10], controlled_buffer_1_out_2[11], controlled_buffer_1_out_2[12], controlled_buffer_1_out_2[13], controlled_buffer_1_out_2[14], controlled_buffer_1_out_2[15]);
  Decoder #(.select(3)) decoder_1 (
    .out0(decoder_1_out0), .out1(decoder_1_out1), .out2(decoder_1_out2), .out3(decoder_1_out3),
    .out4(decoder_1_out4), .out5(decoder_1_out5), .out6(decoder_1_out6), .out7(decoder_1_out7), .sel(e2));  // open: en
  assign Output = decoder_1_out3 ? or_1_out : 16'bz;  // Controlled_Buffer controlled_buffer_6
  assign Output = decoder_1_out4 ? xor_1_out : 16'bz;  // Controlled_Buffer controlled_buffer_7
  assign controlled_buffer_8_out = decoder_1_out5 ? shifter_1_out : 16'bz;  // Controlled_Buffer controlled_buffer_8
  assign controlled_buffer_8_out = decoder_1_out6 ? shifter_2_out : 16'bz;  // Controlled_Buffer controlled_buffer_9
  assign Output = not_2_out ? controlled_buffer_8_out : 16'bz;  // Controlled_Buffer controlled_buffer_10
  not not_2 (not_2_out, or_2_out);
  assign Output = decoder_1_out5 ? controlled_buffer_13_out : 16'bz;  // Controlled_Buffer controlled_buffer_11
  assign Output = decoder_1_out6 ? controlled_buffer_13_out : 16'bz;  // Controlled_Buffer controlled_buffer_12
  assign controlled_buffer_13_out = or_2_out ? {16{1'b0}} : 16'bz;  // Controlled_Buffer controlled_buffer_13
  assign Output = decoder_1_out7 ? multiplier_1_out : 16'bz;  // Controlled_Buffer controlled_buffer_14

  // Notes on the sheet:
  //   dans les deux cas (décalge à droite et à gauche), 
  //   si on décale de 16 bits ou plus, cela revient à avoir
  //   zéro comme sorti, de ce fait si on a un 1 à bit (compris
  //   entre le le numéro 4 le numéro 15) on renverra 0
endmodule

module DecodeIR (
  input  [31:0] IR,
  input  [1:0] in_2,
  input  [31:0] IR_2,
  output WriteReg,
  output WriteReg_2,
  output Store,
  output Load,
  output Load_2,
  output CTRL,
  output CTRL_2,
  output [2:0] GetOp,
  output [15:0] JMPAddress
);

  wire CTRL_t, MEM, not_1_out, not_2_out, not_3_out, not_4_out, not_5_out, not_6_out, not_7_out, not_8_out,
       not_9_out, not_10_out, not_11_out, not_12_out, not_13_out, not_14_out, OP0, OP1, OP2, OP3, OP4, OP5,
       OP6, OP7, UAL;

  not not_1 (not_1_out, in_2[1]);
  not not_2 (not_2_out, in_2[0]);
  and and_1 (UAL, not_1_out, not_2_out);
  and and_2 (CTRL_t, in_2[1], in_2[0]);
  xor xor_1 (MEM, in_2[1], in_2[0]);
  not not_3 (not_3_out, IR_2[28]);
  not not_4 (not_4_out, IR_2[29]);
  not not_5 (not_5_out, IR_2[29]);
  not not_6 (not_6_out, IR_2[27]);
  and and_3 (OP0, not_4_out, not_3_out, not_6_out);
  not not_7 (not_7_out, IR_2[27]);
  not not_8 (not_8_out, IR_2[28]);
  not not_9 (not_9_out, IR_2[29]);
  and and_4 (OP1, not_5_out, not_8_out, IR_2[27]);
  and and_5 (OP2, not_9_out, IR_2[28], not_7_out);
  not not_10 (not_10_out, IR_2[29]);
  not not_11 (not_11_out, IR_2[28]);
  and and_6 (OP4, IR_2[29], not_11_out, not_13_out);
  and and_7 (OP3, not_10_out, IR_2[28], IR_2[27]);
  not not_12 (not_12_out, IR_2[28]);
  not not_13 (not_13_out, IR_2[27]);
  and and_8 (OP5, IR_2[29], not_12_out, IR_2[27]);
  not not_14 (not_14_out, IR_2[27]);
  and and_9 (OP6, IR_2[29], IR_2[28], not_14_out);
  and and_10 (OP7, IR_2[29], IR_2[28], IR_2[27]);

  assign CTRL = 1'b0;
  assign CTRL_2 = 1'b0;
  assign GetOp = 3'b000;
  assign IR_2[31:30] = in_2;
  assign JMPAddress = {16{1'b0}};
  assign Load = 1'b0;
  assign Load_2 = 1'b0;
  assign Store = 1'b0;
  assign WriteReg = 1'b1;
  assign WriteReg_2 = 1'b1;

  // Other names for the same wires on the sheet: CONST[15:0] = IR_2[15:0]; REG_SOURCE2[2:0] = IR_2[19:17];
  //   REG_SOURCE1[2:0] = IR_2[22:20]; REG_DEST[2:0] = IR_2[25:23]; IMMEDIAT = IR_2[26]; OP[2:0] = IR_2[29:27];
  //   INSTR[1:0] = in_2
endmodule

module GetAddr (
  input  [15:0] PC,
  input  Load,
  input  Store,
  input  Fetch,
  output [15:0] Addr
);
endmodule

module GetCst (
  input  [31:0] IR,
  output [15:0] Cst,
  output Imm
);

  Bit_Extender #(.in_width(20)) bit_extender_1 (.in(IR[31:12]), .out(Cst));

  assign Imm = IR[5];
endmodule

module RamCtrl (
  input  Clock,
  input  Exec,
  input  Fetch,
  input  Load,
  input  Store,
  output MemLoad,
  output MemStore
);

  wire and_1_out;

  and and_1 (and_1_out, Exec, Load);
  and and_2 (MemStore, Exec, Clock, Store);
  or or_1 (MemLoad, Fetch, and_1_out);
endmodule

module Registres (
  input  [15:0] IN,
  input  [2:0] SR1,
  input  [2:0] SR2,
  input  WriteReg,
  input  [2:0] DR,
  input  Clock,
  input  Reset,
  output [15:0] R0,
  output [15:0] OUT_SR1,
  output [15:0] R1,
  output [15:0] R2,
  output [15:0] R3,
  output [15:0] OUT_SR2,
  output [15:0] R4,
  output [15:0] R5,
  output [15:0] OUT_DR,
  output [15:0] R6,
  output [15:0] R7
);

  wire DR0, DR1, DR2, DR3, DR4, DR5, DR6, DR7;

  Decoder #(.select(3), .disabled(0)) decoder_1 (
    .out0(DR0), .out1(DR1), .out2(DR2), .out3(DR3), .out4(DR4), .out5(DR5), .out6(DR6), .out7(DR7), .sel(DR),
    .en(WriteReg));
  Register #(.width(16), .trigger("falling")) u_R0 (.D(IN), .en(DR0), .Q(R0), .clk(Clock), .clr(Reset));
  Register #(.width(16), .trigger("falling")) u_R1 (.D(IN), .en(DR1), .Q(R1), .clk(Clock), .clr(Reset));
  Register #(.width(16), .trigger("falling")) u_R2 (.D(IN), .en(DR2), .Q(R2), .clk(Clock), .clr(Reset));
  Register #(.width(16), .trigger("falling")) u_R3 (.D(IN), .en(DR3), .Q(R3), .clk(Clock), .clr(Reset));
  Register #(.width(16), .trigger("falling")) u_R4 (.D(IN), .en(DR4), .Q(R4), .clk(Clock), .clr(Reset));
  Register #(.width(16), .trigger("falling")) u_R5 (.D(IN), .en(DR5), .Q(R5), .clk(Clock), .clr(Reset));
  Register #(.width(16), .trigger("falling")) u_R6 (.D(IN), .en(DR6), .Q(R6), .clk(Clock), .clr(Reset));
  Register #(.width(16), .trigger("falling")) u_R7 (.D(IN), .en(DR7), .Q(R7), .clk(Clock), .clr(Reset));
  Multiplexer #(.select(3), .width(16)) multiplexer_1 (
    .in0(R0), .in1(R1), .in2(R2), .in3(R3), .in4(R4), .in5(R5), .in6(R6), .in7(R7), .out(OUT_SR1), .sel(SR1));  // open: en
  Multiplexer #(.select(3), .width(16)) multiplexer_2 (
    .in0(R0), .in1(R1), .in2(R2), .in3(R3), .in4(R4), .in5(R5), .in6(R6), .in7(R7), .out(OUT_SR2), .sel(SR2));  // open: en
  Multiplexer #(.select(3), .width(16)) multiplexer_3 (
    .in0(R0), .in1(R1), .in2(R2), .in3(R3), .in4(R4), .in5(R5), .in6(R6), .in7(R7), .out(OUT_DR), .sel(DR));  // open: en
endmodule

module RegPC (
  input  [15:0] JMP_Address,
  input  Cond,
  input  CTRL,
  input  Clock,
  input  Reset,
  output [15:0] PC
);

  Register #(.width(16), .trigger("falling")) u_PC (.Q(PC), .clk(Clock), .clr(Reset));  // open: D, en
endmodule

module Seq (
  input  ClockOrig,
  input  reset,
  output Fetch,
  output Exec,
  output Clock
);

  Register #(.width(1), .trigger("falling")) register_1 (
    .D(Fetch), .Q(Exec), .clk(ClockOrig), .clr(reset));  // open: en
  not not_1 (Fetch, Exec);
  buf buffer_1 (Clock, ClockOrig);
endmodule
